# Fritzing sketch wiring (saved by Fritzing 1.0.2b)
breadboards: 1

parts:
  IRLZ44N = MOSFET-NCHANNEL [package=to220v]
  R2 = Resistor [tolerance=±1% resistance=1k power=0.25W package=THT]
  C1 = Electrolytic Capacitor [capacitance=0.1mF voltage=20V package="100 mil [THT, electrolytic]"]
  V1 = DC Power [voltage=12V]
  Raspberry_Pi_4 = Raspberry Pi B+
  USB-C = USB Connectors [package=usb-a-h]
  Motor_Power = DC Power [voltage=12V]
  LED_Ring = NeoPixel Jewel [part_number=2226]
  C2 = Capacitor Polarized [mn=100uF package=panasonic_d]
  part = DRV 8825 Stepper Motor Carrier, High Current [part_number="DRV 8825"]
  NEMA17 = Stepper Motor - Bipolar [mn=40-42]

nets:
  N1: IRLZ44N.G, R2.Pin_1
  N2: IRLZ44N.D, LED_Ring.GND
  N3: IRLZ44N.S, C1.-, V1.V-
  N4: R2.Pin_0, Raspberry_Pi_4.GPIO18
  N5: C1.+, V1.V+
  N6: USB-C.VBUS, Motor_Power.V+, C2.+, part.VOLTAGE_ST/_MT
  N7: USB-C.GND, Motor_Power.V-, C2.-, part.GROUND_ST/_MT, part.GROUND_LOG
  N8: part.RESET, part.SLEEP
  net label: part.STEP, part.DIRECTION
  N9: part.OUT_2B, NEMA17.A
  N10: part.OUT_2A, NEMA17.C
  N11: part.OUT_1A, NEMA17.B
  N12: part.OUT_1B, NEMA17.D

custom parts:
  NeoPixel Jewel: We fit seven of our tiny 5050 (5mm x 5mm) smart RGB LEDs onto a beautiful, round PCB with mounting holes and a chainable design to create what we think is our most elegant (and evening-wear appropriate) NeoPixel board yet. Use only one microcontroller pin to control as many as you can chain together! Each LED is addressable as the driver chip is inside the LED. Each one has ~18mA constant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
